// Logisim project clock cs21b042.circ as structural Verilog: 6 circuits, main circuit 24 HR CLOCK
module main (
);

  wire and_1_out, and_2_out, and_3_out, and_4_out, and_5_out, clock_1_out, n3_counter_1_a1, n3_counter_1_a2,
       n6_counter_1_b1, n6_counter_1_b2, n6_counter_1_b3, n6_counter_1_out6, n6_counter_2_b1,
       n6_counter_2_b2, n6_counter_2_b3, n6_counter_2_out6, n7_segment_1_a_2, n7_segment_1_b_2,
       n7_segment_1_c_2, n7_segment_1_d_2, n7_segment_1_e, n7_segment_1_f, n7_segment_1_g, n7_segment_2_a_2,
       n7_segment_2_b_2, n7_segment_2_c_2, n7_segment_2_d_2, n7_segment_2_e, n7_segment_2_f, n7_segment_2_g,
       n7_segment_3_a_2, n7_segment_3_b_2, n7_segment_3_c_2, n7_segment_3_d_2, n7_segment_3_e,
       n7_segment_3_f, n7_segment_3_g, n7_segment_4_a_2, n7_segment_4_b_2, n7_segment_4_c_2,
       n7_segment_4_d_2, n7_segment_4_e, n7_segment_4_f, n7_segment_4_g, n7_segment_5_a_2, n7_segment_5_b_2,
       n7_segment_5_c_2, n7_segment_5_d_2, n7_segment_5_e, n7_segment_5_f, n7_segment_5_g, n7_segment_6_a_2,
       n7_segment_6_b_2, n7_segment_6_c_2, n7_segment_6_d_2, n7_segment_6_e, n7_segment_6_f, n7_segment_6_g,
       n10_counter_1_a1, n10_counter_1_a2, n10_counter_1_a3, n10_counter_1_a4, n10_counter_1_out1,
       n10_counter_2_a1, n10_counter_2_a2, n10_counter_2_a3, n10_counter_2_a4, n10_counter_2_out1,
       n10_counter_3_a1, n10_counter_3_a2, n10_counter_3_a3, n10_counter_3_a4, n10_counter_3_out1, not_1_out,
       not_2_out, not_3_out, not_4_out;

  _7_Segment_Display u_7_segment_display_1 (
    .g(n7_segment_1_g), .f(n7_segment_1_f), .a(n7_segment_1_a_2), .b(n7_segment_1_b_2), .e(n7_segment_1_e),
    .d(n7_segment_1_d_2), .c(n7_segment_1_c_2));  // open: dp
  _7_segment u_7_segment_1 (
    .A(1'b0), .B(1'b0), .C(n3_counter_1_a1), .D(n3_counter_1_a2), .a_2(n7_segment_1_a_2),
    .b_2(n7_segment_1_b_2), .c_2(n7_segment_1_c_2), .d_2(n7_segment_1_d_2), .e(n7_segment_1_e),
    .f(n7_segment_1_f), .g(n7_segment_1_g));
  _3_counter u_3_counter_1 (
    .reset3(and_2_out), .a1(n3_counter_1_a1), .a2(n3_counter_1_a2), .clk(clock_1_out), .en(and_1_out));
  and and_1 (and_1_out, n10_counter_1_out1, and_3_out);
  _7_Segment_Display u_7_segment_display_2 (
    .g(n7_segment_2_g), .f(n7_segment_2_f), .a(n7_segment_2_a_2), .b(n7_segment_2_b_2), .e(n7_segment_2_e),
    .d(n7_segment_2_d_2), .c(n7_segment_2_c_2));  // open: dp
  _7_segment u_7_segment_2 (
    .A(n10_counter_1_a1), .B(n10_counter_1_a2), .C(n10_counter_1_a3), .D(n10_counter_1_a4),
    .a_2(n7_segment_2_a_2), .b_2(n7_segment_2_b_2), .c_2(n7_segment_2_c_2), .d_2(n7_segment_2_d_2),
    .e(n7_segment_2_e), .f(n7_segment_2_f), .g(n7_segment_2_g));
  _10_counter u_10_counter_1 (
    .en(and_3_out), .reset10(and_2_out), .a1(n10_counter_1_a1), .a2(n10_counter_1_a2),
    .out1(n10_counter_1_out1), .a3(n10_counter_1_a3), .a4(n10_counter_1_a4), .clk(clock_1_out));
  and and_2 (and_2_out, n3_counter_1_a1, n10_counter_1_a2, not_2_out, not_3_out, not_4_out);
  not not_1 (not_1_out, n3_counter_1_a2);
  not not_2 (not_2_out, n10_counter_1_a1);
  not not_3 (not_3_out, n10_counter_1_a3);
  not not_4 (not_4_out, n10_counter_1_a4);
  and and_3 (and_3_out, n6_counter_1_out6, and_4_out);
  and and_4 (and_4_out, n10_counter_2_out1, and_5_out);
  _7_Segment_Display u_7_segment_display_3 (
    .g(n7_segment_3_g), .f(n7_segment_3_f), .a(n7_segment_3_a_2), .b(n7_segment_3_b_2), .e(n7_segment_3_e),
    .d(n7_segment_3_d_2), .c(n7_segment_3_c_2));  // open: dp
  _7_segment u_7_segment_3 (
    .A(1'b0), .B(n6_counter_1_b1), .C(n6_counter_1_b2), .D(n6_counter_1_b3), .a_2(n7_segment_3_a_2),
    .b_2(n7_segment_3_b_2), .c_2(n7_segment_3_c_2), .d_2(n7_segment_3_d_2), .e(n7_segment_3_e),
    .f(n7_segment_3_f), .g(n7_segment_3_g));
  _6_counter u_6_counter_1 (
    .en(and_4_out), .reset6(and_2_out), .OUT6(n6_counter_1_out6), .b3(n6_counter_1_b3), .b2(n6_counter_1_b2),
    .b1(n6_counter_1_b1), .in2(clock_1_out));
  _7_Segment_Display u_7_segment_display_4 (
    .g(n7_segment_4_g), .f(n7_segment_4_f), .a(n7_segment_4_a_2), .b(n7_segment_4_b_2), .e(n7_segment_4_e),
    .d(n7_segment_4_d_2), .c(n7_segment_4_c_2));  // open: dp
  _7_segment u_7_segment_4 (
    .A(n10_counter_2_a1), .B(n10_counter_2_a2), .C(n10_counter_2_a3), .D(n10_counter_2_a4),
    .a_2(n7_segment_4_a_2), .b_2(n7_segment_4_b_2), .c_2(n7_segment_4_c_2), .d_2(n7_segment_4_d_2),
    .e(n7_segment_4_e), .f(n7_segment_4_f), .g(n7_segment_4_g));
  _10_counter u_10_counter_2 (
    .en(and_5_out), .reset10(and_2_out), .a1(n10_counter_2_a1), .a2(n10_counter_2_a2),
    .out1(n10_counter_2_out1), .a3(n10_counter_2_a3), .a4(n10_counter_2_a4), .clk(clock_1_out));
  and and_5 (and_5_out, n6_counter_2_out6, n10_counter_3_out1);
  _7_Segment_Display u_7_segment_display_5 (
    .g(n7_segment_5_g), .f(n7_segment_5_f), .a(n7_segment_5_a_2), .b(n7_segment_5_b_2), .e(n7_segment_5_e),
    .d(n7_segment_5_d_2), .c(n7_segment_5_c_2));  // open: dp
  _7_segment u_7_segment_5 (
    .A(1'b0), .B(n6_counter_2_b1), .C(n6_counter_2_b2), .D(n6_counter_2_b3), .a_2(n7_segment_5_a_2),
    .b_2(n7_segment_5_b_2), .c_2(n7_segment_5_c_2), .d_2(n7_segment_5_d_2), .e(n7_segment_5_e),
    .f(n7_segment_5_f), .g(n7_segment_5_g));
  _6_counter u_6_counter_2 (
    .en(n10_counter_3_out1), .reset6(and_2_out), .OUT6(n6_counter_2_out6), .b3(n6_counter_2_b3),
    .b2(n6_counter_2_b2), .b1(n6_counter_2_b1), .in2(clock_1_out));
  _7_Segment_Display u_7_segment_display_6 (
    .g(n7_segment_6_g), .f(n7_segment_6_f), .a(n7_segment_6_a_2), .b(n7_segment_6_b_2), .e(n7_segment_6_e),
    .d(n7_segment_6_d_2), .c(n7_segment_6_c_2));  // open: dp
  _7_segment u_7_segment_6 (
    .A(n10_counter_3_a1), .B(n10_counter_3_a2), .C(n10_counter_3_a3), .D(n10_counter_3_a4),
    .a_2(n7_segment_6_a_2), .b_2(n7_segment_6_b_2), .c_2(n7_segment_6_c_2), .d_2(n7_segment_6_d_2),
    .e(n7_segment_6_e), .f(n7_segment_6_f), .g(n7_segment_6_g));
  _10_counter u_10_counter_3 (
    .en(1'b1), .reset10(and_2_out), .a1(n10_counter_3_a1), .a2(n10_counter_3_a2), .out1(n10_counter_3_out1),
    .a3(n10_counter_3_a3), .a4(n10_counter_3_a4), .clk(clock_1_out));
  _7_Segment_Display u_7_segment_display_7 (.g(1'b1), .f(1'b1), .e(1'b1), .c(1'b1));  // open: a, b, d, dp
  _7_Segment_Display u_7_segment_display_8 (.g(1'b1), .e(1'b1));  // open: f, a, b, d, c, dp
  Clock clock_1 (.out(clock_1_out));
endmodule

module _10_counter (
  input  en,
  input  clk,
  input  reset10,
  output a1,
  output a2,
  output a3,
  output a4,
  output out1
);

  wire A_qn, and_2_out, and_3_out, and_4_out, and_5_out, and_6_out, and_7_out, and_8_out, B_qn, C_qn, D_qn,
       not_1_out, not_2_out, or_1_out, or_2_out, or_3_out;

  and and_1 (out1, a4, not_1_out, a1, not_2_out);
  or or_1 (or_1_out, and_4_out, and_6_out, and_5_out);
  not not_1 (not_1_out, a3);
  not not_2 (not_2_out, a2);
  and and_2 (and_2_out, D_qn, a1);
  and and_3 (and_3_out, a3, a2, a4);
  and and_4 (and_4_out, C_qn, a2);
  and and_5 (and_5_out, a4, a3, B_qn);
  and and_6 (and_6_out, D_qn, a2);
  or or_2 (or_2_out, and_2_out, and_3_out);
  D_Flip_Flop A (.clk(clk), .D(or_2_out), .Q(a1), .Qn(A_qn), .en(en), .reset(reset10));  // open: preset
  D_Flip_Flop B (.clk(clk), .D(or_1_out), .Q(a2), .Qn(B_qn), .en(en), .reset(reset10));  // open: preset
  and and_7 (and_7_out, A_qn, a4, C_qn);
  or or_3 (or_3_out, and_7_out, and_8_out);
  and and_8 (and_8_out, D_qn, a3);
  D_Flip_Flop C (.clk(clk), .D(or_3_out), .Q(a3), .Qn(C_qn), .en(en), .reset(reset10));  // open: preset
  D_Flip_Flop D (.clk(clk), .D(D_qn), .Q(a4), .Qn(D_qn), .en(en), .reset(reset10));  // open: preset
endmodule

module _6_counter (
  input  en,
  input  in2,
  input  reset6,
  output OUT6,
  output b3,
  output b2,
  output b1
);

  wire A_qn, and_1_out, and_2_out, and_3_out, and_4_out, B_qn, C_qn, not_1_out, or_1_out, or_2_out;

  and and_1 (and_1_out, b2, b3);
  and and_2 (and_2_out, b1, C_qn);
  D_Flip_Flop A (.clk(in2), .D(or_1_out), .Q(b1), .Qn(A_qn), .en(en), .reset(reset6));  // open: preset
  or or_1 (or_1_out, and_1_out, and_2_out);
  and and_3 (and_3_out, C_qn, b2);
  or or_2 (or_2_out, and_3_out, and_4_out);
  and and_4 (and_4_out, B_qn, A_qn, b3);
  D_Flip_Flop B (.clk(in2), .D(or_2_out), .Q(b2), .Qn(B_qn), .en(en), .reset(reset6));  // open: preset
  D_Flip_Flop C (.clk(in2), .D(C_qn), .Q(b3), .Qn(C_qn), .en(en), .reset(reset6));  // open: preset
  not not_1 (not_1_out, b2);
  and and_5 (OUT6, not_1_out, b1, b3);
endmodule

module _3_counter (
  input  reset3,
  input  clk,
  input  en,
  output a1,
  output a2
);

  wire A_qn, and_1_out, B_qn;

  D_Flip_Flop A (.clk(clk), .D(a2), .Q(a1), .Qn(A_qn), .en(en), .reset(reset3));  // open: preset
  and and_1 (and_1_out, A_qn, B_qn);
  D_Flip_Flop B (.clk(clk), .D(and_1_out), .Q(a2), .Qn(B_qn), .en(en), .reset(reset3));  // open: preset
endmodule

module _7_segment (
  input  A,
  input  B,
  input  C,
  input  D,
  output a_2,
  output b_2,
  output c_2,
  output d_2,
  output e,
  output f,
  output g
);

  wire and_1_out, and_2_out, and_3_out, and_4_out, and_5_out, and_6_out, and_7_out, and_8_out, and_9_out,
       and_10_out, and_11_out, and_12_out, and_13_out, and_14_out, and_15_out, and_16_out, not_1_out,
       not_2_out, not_3_out, not_4_out, not_5_out, not_6_out, not_7_out, not_8_out, not_9_out, not_10_out,
       not_11_out, not_12_out, not_13_out, not_14_out, not_15_out, not_16_out, not_17_out, not_18_out,
       not_19_out, not_20_out, not_21_out;

  not not_1 (not_1_out, B);
  and and_1 (and_1_out, not_1_out, not_2_out);
  not not_2 (not_2_out, D);
  and and_2 (and_2_out, B, D);
  not not_3 (not_3_out, B);
  not not_4 (not_4_out, C);
  and and_3 (and_3_out, not_4_out, not_5_out);
  not not_5 (not_5_out, D);
  and and_4 (and_4_out, C, D);
  not not_6 (not_6_out, C);
  or or_1 (c_2, not_6_out, D, B);
  not not_7 (not_7_out, B);
  and and_5 (and_5_out, not_7_out, not_8_out);
  not not_8 (not_8_out, D);
  not not_9 (not_9_out, B);
  and and_6 (and_6_out, not_9_out, C);
  and and_7 (and_7_out, C, not_10_out);
  not not_10 (not_10_out, D);
  not not_11 (not_11_out, C);
  and and_8 (and_8_out, B, not_11_out, D);
  not not_12 (not_12_out, B);
  and and_9 (and_9_out, not_12_out, not_13_out);
  not not_13 (not_13_out, D);
  and and_10 (and_10_out, C, not_14_out);
  not not_14 (not_14_out, D);
  not not_15 (not_15_out, C);
  and and_11 (and_11_out, not_15_out, not_16_out);
  not not_16 (not_16_out, D);
  and and_12 (and_12_out, B, not_17_out);
  not not_17 (not_17_out, C);
  and and_13 (and_13_out, B, not_18_out);
  not not_18 (not_18_out, D);
  not not_19 (not_19_out, B);
  and and_14 (and_14_out, not_19_out, C);
  and and_15 (and_15_out, B, not_20_out);
  not not_20 (not_20_out, C);
  and and_16 (and_16_out, B, not_21_out);
  not not_21 (not_21_out, D);
  or or_2 (a_2, and_1_out, C, and_2_out, A);
  or or_3 (b_2, not_3_out, and_3_out, and_4_out);
  or or_4 (d_2, and_5_out, and_6_out, and_7_out, and_8_out, A);
  or or_5 (e, and_9_out, and_10_out);
  or or_6 (f, and_11_out, and_12_out, and_13_out, A);
  or or_7 (g, and_14_out, and_15_out, and_16_out, A);
endmodule

module _24_HR_CLOCK (
  input  SET_CLOCK
);

  wire and_1_out, and_2_out, and_3_out, and_4_out, c_2_out, c_3_out, c_4_out, c_out, clock_1_out, h_out,
       m_out, n3_counter_1_a1, n3_counter_1_a2, n6_counter_1_b1, n6_counter_1_b2, n6_counter_1_b3,
       n6_counter_1_out6, n6_counter_2_b1, n6_counter_2_b2, n6_counter_2_b3, n6_counter_2_out6,
       n7_segment_1_a_2, n7_segment_1_b_2, n7_segment_1_c_2, n7_segment_1_d_2, n7_segment_1_e,
       n7_segment_1_f, n7_segment_1_g, n7_segment_2_a_2, n7_segment_2_b_2, n7_segment_2_c_2,
       n7_segment_2_d_2, n7_segment_2_e, n7_segment_2_f, n7_segment_2_g, n7_segment_3_a_2, n7_segment_3_b_2,
       n7_segment_3_c_2, n7_segment_3_d_2, n7_segment_3_e, n7_segment_3_f, n7_segment_3_g, n7_segment_4_a_2,
       n7_segment_4_b_2, n7_segment_4_c_2, n7_segment_4_d_2, n7_segment_4_e, n7_segment_4_f, n7_segment_4_g,
       n7_segment_5_a_2, n7_segment_5_b_2, n7_segment_5_c_2, n7_segment_5_d_2, n7_segment_5_e,
       n7_segment_5_f, n7_segment_5_g, n7_segment_6_a_2, n7_segment_6_b_2, n7_segment_6_c_2,
       n7_segment_6_d_2, n7_segment_6_e, n7_segment_6_f, n7_segment_6_g, n10_counter_1_a1, n10_counter_1_a2,
       n10_counter_1_a3, n10_counter_1_a4, n10_counter_1_out1, n10_counter_2_a1, n10_counter_2_a2,
       n10_counter_2_a3, n10_counter_2_a4, n10_counter_2_out1, n10_counter_3_a1, n10_counter_3_a2,
       n10_counter_3_a3, n10_counter_3_a4, n10_counter_3_out1, not_1_out, not_2_out, not_3_out, not_4_out,
       not_5_out, or_1_out, or_2_out, or_3_out, or_4_out, or_5_out, or_6_out, or_7_out, or_8_out, or_9_out,
       or_10_out, or_11_out, RESET_out, s_out;

  or or_1 (or_1_out, c_out, and_1_out);
  _7_Segment_Display u_7_segment_display_1 (
    .g(n7_segment_1_g), .f(n7_segment_1_f), .a(n7_segment_1_a_2), .b(n7_segment_1_b_2), .e(n7_segment_1_e),
    .d(n7_segment_1_d_2), .c(n7_segment_1_c_2));  // open: dp
  _7_segment u_7_segment_1 (
    .A(1'b0), .B(1'b0), .C(n3_counter_1_a1), .D(n3_counter_1_a2), .a_2(n7_segment_1_a_2),
    .b_2(n7_segment_1_b_2), .c_2(n7_segment_1_c_2), .d_2(n7_segment_1_d_2), .e(n7_segment_1_e),
    .f(n7_segment_1_f), .g(n7_segment_1_g));
  _3_counter u_3_counter_1 (
    .reset3(or_5_out), .a1(n3_counter_1_a1), .a2(n3_counter_1_a2), .clk(or_2_out), .en(or_1_out));
  and and_1 (and_1_out, n10_counter_1_out1, SET_CLOCK);
  and c (c_out, n10_counter_1_out1, or_3_out);
  _7_Segment_Display u_7_segment_display_2 (
    .g(n7_segment_2_g), .f(n7_segment_2_f), .a(n7_segment_2_a_2), .b(n7_segment_2_b_2), .e(n7_segment_2_e),
    .d(n7_segment_2_d_2), .c(n7_segment_2_c_2));  // open: dp
  _7_segment u_7_segment_2 (
    .A(n10_counter_1_a1), .B(n10_counter_1_a2), .C(n10_counter_1_a3), .D(n10_counter_1_a4),
    .a_2(n7_segment_2_a_2), .b_2(n7_segment_2_b_2), .c_2(n7_segment_2_c_2), .d_2(n7_segment_2_d_2),
    .e(n7_segment_2_e), .f(n7_segment_2_f), .g(n7_segment_2_g));
  or or_2 (or_2_out, or_4_out, and_4_out);
  or or_3 (or_3_out, SET_CLOCK, c_2_out);
  _10_counter u_10_counter_1 (
    .en(or_3_out), .reset10(or_5_out), .a1(n10_counter_1_a1), .a2(n10_counter_1_a2),
    .out1(n10_counter_1_out1), .a3(n10_counter_1_a3), .a4(n10_counter_1_a4), .clk(or_4_out));
  or or_4 (or_4_out, h_out, and_4_out);
  or or_5 (or_5_out, RESET_out, and_2_out);
  and and_2 (and_2_out, n3_counter_1_a1, n10_counter_1_a2, not_2_out, not_3_out, not_4_out);
  not not_1 (not_1_out, n3_counter_1_a2);
  not not_2 (not_2_out, n10_counter_1_a1);
  not not_3 (not_3_out, n10_counter_1_a3);
  not not_4 (not_4_out, n10_counter_1_a4);
  Button h (.out(h_out));
  and c_2 (c_2_out, n6_counter_1_out6, or_6_out);
  Button RESET (.out(RESET_out));
  or or_6 (or_6_out, c_3_out, and_3_out);
  _7_Segment_Display u_7_segment_display_3 (
    .g(n7_segment_3_g), .f(n7_segment_3_f), .a(n7_segment_3_a_2), .b(n7_segment_3_b_2), .e(n7_segment_3_e),
    .d(n7_segment_3_d_2), .c(n7_segment_3_c_2));  // open: dp
  _7_segment u_7_segment_3 (
    .A(1'b0), .B(n6_counter_1_b1), .C(n6_counter_1_b2), .D(n6_counter_1_b3), .a_2(n7_segment_3_a_2),
    .b_2(n7_segment_3_b_2), .c_2(n7_segment_3_c_2), .d_2(n7_segment_3_d_2), .e(n7_segment_3_e),
    .f(n7_segment_3_f), .g(n7_segment_3_g));
  _6_counter u_6_counter_1 (
    .en(or_6_out), .reset6(or_5_out), .OUT6(n6_counter_1_out6), .b3(n6_counter_1_b3), .b2(n6_counter_1_b2),
    .b1(n6_counter_1_b1), .in2(or_7_out));
  or or_7 (or_7_out, or_9_out, and_4_out);
  and c_3 (c_3_out, n10_counter_2_out1, c_4_out);
  and and_3 (and_3_out, n10_counter_2_out1, SET_CLOCK);
  _7_Segment_Display u_7_segment_display_4 (
    .g(n7_segment_4_g), .f(n7_segment_4_f), .a(n7_segment_4_a_2), .b(n7_segment_4_b_2), .e(n7_segment_4_e),
    .d(n7_segment_4_d_2), .c(n7_segment_4_c_2));  // open: dp
  _7_segment u_7_segment_4 (
    .A(n10_counter_2_a1), .B(n10_counter_2_a2), .C(n10_counter_2_a3), .D(n10_counter_2_a4),
    .a_2(n7_segment_4_a_2), .b_2(n7_segment_4_b_2), .c_2(n7_segment_4_c_2), .d_2(n7_segment_4_d_2),
    .e(n7_segment_4_e), .f(n7_segment_4_f), .g(n7_segment_4_g));
  _10_counter u_10_counter_2 (
    .en(or_8_out), .reset10(or_5_out), .a1(n10_counter_2_a1), .a2(n10_counter_2_a2),
    .out1(n10_counter_2_out1), .a3(n10_counter_2_a3), .a4(n10_counter_2_a4), .clk(or_9_out));
  or or_8 (or_8_out, c_4_out, SET_CLOCK);
  or or_9 (or_9_out, m_out, and_4_out);
  Button m (.out(m_out));
  and c_4 (c_4_out, n6_counter_2_out6, n10_counter_3_out1);
  _7_Segment_Display u_7_segment_display_5 (
    .g(n7_segment_5_g), .f(n7_segment_5_f), .a(n7_segment_5_a_2), .b(n7_segment_5_b_2), .e(n7_segment_5_e),
    .d(n7_segment_5_d_2), .c(n7_segment_5_c_2));  // open: dp
  _7_segment u_7_segment_5 (
    .A(1'b0), .B(n6_counter_2_b1), .C(n6_counter_2_b2), .D(n6_counter_2_b3), .a_2(n7_segment_5_a_2),
    .b_2(n7_segment_5_b_2), .c_2(n7_segment_5_c_2), .d_2(n7_segment_5_d_2), .e(n7_segment_5_e),
    .f(n7_segment_5_f), .g(n7_segment_5_g));
  _6_counter u_6_counter_2 (
    .en(n10_counter_3_out1), .reset6(or_5_out), .OUT6(n6_counter_2_out6), .b3(n6_counter_2_b3),
    .b2(n6_counter_2_b2), .b1(n6_counter_2_b1), .in2(or_10_out));
  or or_10 (or_10_out, or_11_out, and_4_out);
  _7_Segment_Display u_7_segment_display_6 (
    .g(n7_segment_6_g), .f(n7_segment_6_f), .a(n7_segment_6_a_2), .b(n7_segment_6_b_2), .e(n7_segment_6_e),
    .d(n7_segment_6_d_2), .c(n7_segment_6_c_2));  // open: dp
  _7_segment u_7_segment_6 (
    .A(n10_counter_3_a1), .B(n10_counter_3_a2), .C(n10_counter_3_a3), .D(n10_counter_3_a4),
    .a_2(n7_segment_6_a_2), .b_2(n7_segment_6_b_2), .c_2(n7_segment_6_c_2), .d_2(n7_segment_6_d_2),
    .e(n7_segment_6_e), .f(n7_segment_6_f), .g(n7_segment_6_g));
  _10_counter u_10_counter_3 (
    .en(1'b1), .reset10(or_5_out), .a1(n10_counter_3_a1), .a2(n10_counter_3_a2), .out1(n10_counter_3_out1),
    .a3(n10_counter_3_a3), .a4(n10_counter_3_a4), .clk(or_11_out));
  or or_11 (or_11_out, s_out, and_4_out);
  _7_Segment_Display u_7_segment_display_7 (.g(1'b1), .e(1'b1));  // open: f, a, b, d, c, dp
  _7_Segment_Display u_7_segment_display_8 (.g(1'b1), .f(1'b1), .e(1'b1), .c(1'b1));  // open: a, b, d, dp
  Button s (.out(s_out));
  and and_4 (and_4_out, not_5_out, clock_1_out);
  not not_5 (not_5_out, SET_CLOCK);
  Clock clock_1 (.out(clock_1_out));

  // Notes on the sheet:
  //   HOURS
  //   MINUTES
  //   SECONDS
endmodule
